# Fritzing sketch schm-20.5.8_Caixa_Steck (saved by Fritzing 0.9.4)
breadboards: 1

parts:
  ESP8266-nodemcu = NodeMCU V1.0
  Fonte_AC/DC_5V = HLK-PM01
  releLampEscada = KY-019 5V Relay Module [package="Breakout board"]
  ReleLampTelhado = KY-019 5V Relay Module [package="Breakout board"]
  releBuzzer = KY-019 5V Relay Module [package="Breakout board"]
  Rele1 = KY-019 5V Relay Module [package="Breakout board"]
  Fusível_1A = FUSE [package=fuse_5mm]
  J1 = Screw terminal - 2 pins [package=THT]
  Led_Piloto = LED - 5mm [color="Red (633nm)" package="5 mm [THT]"]
  Sensor_de_presença_-_PIR = HC-SR501 Body Sensor Module
  DHT1 = DHT11 Humidity and Temperature Sensor
  Entrada_-_Fio_soldado = Screw terminal - 2 pins [package=THT]
  Buzzer = Buzzer 12mm [package=buzzer-ccv-kit]
  R1 = Resistor [tolerance=±5% resistance=100 package=THT]

nets:
  N1: ESP8266-nodemcu.D0, Sensor_de_presença_-_PIR.OUT
  N2: ESP8266-nodemcu.D1, Entrada_-_Fio_soldado.pin1
  N3: ESP8266-nodemcu.D2, R1.Pin_0
  N4: ESP8266-nodemcu.D4, DHT1.DATA
  3V3: ESP8266-nodemcu.3V3, Sensor_de_presença_-_PIR.VCC, DHT1.VDD
  GND: ESP8266-nodemcu.GND, Fonte_AC/DC_5V.-Vo, releLampEscada.-, ReleLampTelhado.-, releBuzzer.-, Rele1.-, Led_Piloto.cathode, Sensor_de_presença_-_PIR.GND, DHT1.GND, Buzzer.2
  N5: ESP8266-nodemcu.D5, Rele1.S
  N6: ESP8266-nodemcu.D6, releBuzzer.S
  N7: ESP8266-nodemcu.D7, ReleLampTelhado.S
  N8: ESP8266-nodemcu.D8, releLampEscada.S
  N9: ESP8266-nodemcu.Vin, Fonte_AC/DC_5V.+Vo, releLampEscada.+, ReleLampTelhado.+, releBuzzer.+, releBuzzer.Common, Rele1.+
  N10: Fonte_AC/DC_5V.AC#0, Fusível_1A.2
  N11: Fonte_AC/DC_5V.AC#1, J1.pin2
  N12: releBuzzer.NO, Buzzer.1
  N13: Fusível_1A.1, J1.pin1
  N14: Led_Piloto.anode, R1.Pin_1

custom parts:
  NodeMCU V1.0: ESP8266 based NodeMCU
  KY-019 5V Relay Module: KY-019 5V Relay module, used to control AC circuits.
  HC-SR501 Body Sensor Module: Pyroelectric Infrared PIR Motion Sensor Detector Module
  DHT11 Humidity and Temperature Sensor: DHT22 Humidity and Temperature Sensor
