# Fritzing sketch schm-20.04.30 (saved by Fritzing 0.9.4)
breadboards: 1

parts:
  U1 = NodeMCU V1.0
  HLK-PM1 = HLK-PM01
  Rele1 = KY-019 5V Relay Module [package="Breakout board"]
  Rele2 = KY-019 5V Relay Module [package="Breakout board"]
  Rele3 = KY-019 5V Relay Module [package="Breakout board"]
  Rele4 = KY-019 5V Relay Module [package="Breakout board"]
  F1 = FUSE [package=fuse_5mm]
  J1 = Screw terminal - 2 pins [package=THT]

nets:
  N1: U1.GND, HLK-PM1.-Vo, Rele1.-, Rele2.-, Rele3.-, Rele4.-
  N2: U1.Vin, HLK-PM1.+Vo, Rele1.+, Rele2.+, Rele3.+, Rele4.+
  N3: HLK-PM1.AC#0, F1.2
  N4: HLK-PM1.AC#1, J1.pin2
  N5: F1.1, J1.pin1

custom parts:
  NodeMCU V1.0: ESP8266 based NodeMCU
  KY-019 5V Relay Module: KY-019 5V Relay module, used to control AC circuits.
